# Fritzing sketch shemas cablage (saved by Fritzing 0.9.3b)
breadboards: 1

parts:
  Composant1 = Arduino Mega 2560 (Rev3)
  LED1 = LEDs [package=led10mm]
  U1 = RELAY [package=relay-jzc]
  U2 = RELAY [package=relay-jzc]
  M1 = DC Motor
  S1 = Pushbutton [package="[THT]"]
  S2 = Pushbutton [package="[THT]"]
  J2 = Basic Servo
  R1 = Photocell (LDR) [package=THT]
  RHT1 = Humidity and Temperature Sensor RHT03
  Composant2 = Soil Moisture Sensor
  LED2 = LEDs [package=led10mm]
  U3 = RELAY [package=relay-jzc]

nets:
  N1: Composant1.A8, Composant2.SIG
  N2: Composant1.A0, R1.pin_0
  N3: Composant1.A3, RHT1.GND_2
  N4: Composant1.D13_PWM, U3.NC
  N5: Composant1.D12_PWM, J2.pulse
  GND: Composant1.D11_PWM, Composant1.GND, Composant1.D7_PWM, LED1.C, U1.NO, U2.NO, M1.pin_2, S1.Pin_1, S1.Pin_2, S2.Pin_1, S2.Pin_2, J2.gnd, R1.pin_1, RHT1.Data-signal, Composant2.GND, LED2.A, U3.NO
  N6: Composant1.D10_PWM, U2.NC
  N7: Composant1.D8_PWM, U1.NC
  VCC: Composant1.5V, U1.COIL2, U1.COIL1, U2.COIL2, U2.MAIN, S1.Pin_3, S1.Pin_4, S2.Pin_3, S2.Pin_4, J2.vcc, RHT1.Vcc, Composant2.VCC, U3.COIL2, U3.MAIN
  N8: LED1.A, U1.MAIN
  N9: U2.COIL1, M1.pin_1
  N10: LED2.C, U3.COIL1

notes:
  pompe hydrolique
  Bandeau led
  Relay
  bouton eau - pin 7
  bouton ouverture - pin 11
  Détecteur d'humidité dans le sol
  résistance chauffante
